# Fritzing sketch sketch (saved by Fritzing 0.9.4)
breadboards: 1

parts:
  Part2 = Adafruit LM3671 Buck Converter [part_number="Adafruit #2745"]
  SONAR1 = Maxbotix MaxSonar Ultrasonic Sensor
  Part3 = Grasshopper LoRa/LoRaWAN Development Board
  U1 = LIPO-2000mAh [package=lipo-2000]

nets:
  N1: Part2.EN, Part3.A0
  VIN: Part2.VIN, Part3.3V3
  3.3V: Part2.3.3V, SONAR1.+5V
  N2: SONAR1.GND, Part3.GND#18
  N3: SONAR1.TX, Part3.SCL
  N4: SONAR1.RX, Part3.SDA
  N5: Part3.3, Part3.+, U1.+
  N6: Part3.4, Part3.-, U1.-

notes:
  MaxBotix MB1242
  SDA SCL V+ GND

custom parts:
  Adafruit LM3671 Buck Converter: Your power supply problems just got SUPER SOLVED! This 3.3V Buck Converter Breakout board is great for supplying power to low voltage circuits from a single Li-Ion cell battery or USB power. This chip provides up to 600-mA load current across the entire input voltage range of 3.5 to 5.5V. Great for your portable project, we made this "pin compatible" with the LM1117-3.3V TO-220 chip so you can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
  Maxbotix MaxSonar Ultrasonic Sensor: Maxbotix MaxSonar Ultrasonic Sensor LV-EZ0, LV-EZ1, LV-EZ2, LV-EZ3, LV-EZ4
  Grasshopper LoRa/LoRaWAN Development Board: Grasshopper is a small (0.71 " x 1.76") development board with Murata's CMWX1ZZABZ-078 FCC certified module containing ST Microelectronics' STM32L082 32 MHz Cortex M0+ MCU with 192 kByte of flash and 20 kBytes of RAM and Sematech's SX1276 LoRa radio. The development board exposes 19 GPIOs to the user as well as 3V3, GND, VIN, and VREF (for the analog sector), has an indicator led on GPIO 13 as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
